# Fritzing sketch remot_fan (saved by Fritzing 0.9.3b)
breadboards: 1

parts:
  元件1 = Arduino Uno (Rev3)
  U1 = LCD-16X2 [package=lcd-16x2_noholes]
  LED2 = RGB LED - (4 legs) [package="5 mm [THT]"]
  M1 = DC Motor
  U2 = Stepper Motor Driver-v1.0 [package="DIP28 [THT]"]
  Raspberry_Pi_1 = Raspberry Pi 3 [part_number=RPI-3-V1.2]  # not connected
  VCC1 = Battery  # not connected

nets:
  N1: 元件1.A4/SDA, U1.SDA
  N2: 元件1.A5/SCL, U1.SCL
  N3: 元件1.D9_PWM, U2.IN3
  N4: 元件1.D10_PWM/SS, U2.IN4
  N5: 元件1.D5_PWM, LED2.red_cathode
  N6: 元件1.D6_PWM, LED2.green_cathode
  N7: 元件1.D7, LED2.blue_cathode
  5V: 元件1.5V, U1.VCC, U2.+
  GND: 元件1.GND, U1.GND, LED2.GND, U2.-
  N8: M1.pin_1, U2.OUT4
  N9: M1.pin_2, U2.COM

custom parts:
  LCD-16X2: I2C_LCD1602
  RGB LED - (4 legs): A 5mm tri-color LED with red, green and blue inside.
  Stepper Motor Driver-v1.0: Stepper Motor Driver
